# Fritzing sketch All_in_one_example_wiring (saved by Fritzing 0.9.3b)
breadboards: 1

parts:
  Pico = Raspberry Pi Pico
  RUN = Momentary Switch [package=ksa_sealed_tac_switch]
  START/STOP = Momentary Switch [package=ksa_sealed_tac_switch]
  POT = POT [package=alps_pot]
  LEVEL_SHIFTER = I2C level shifter bidirectional
  I2C_LCD_DISPLAY = LCD1602-I2C
  SD_CARD_MODULE = Full Size SD Card Module

nets:
  N1: Pico.pin_1, Pico.pin_7
  N2: Pico.pin_2, Pico.pin_6
  N3: Pico.pin_3, Pico.pin_8, Pico.pin_13, Pico.pin_18, Pico.pin_23, Pico.pin_28, Pico.pin_33, Pico.pin_38, Pico.pin_42, RUN.1, POT.E, SD_CARD_MODULE.pin_1, SD_CARD_MODULE.pin_16
  N4: Pico.pin_11, LEVEL_SHIFTER.LV4
  N5: Pico.pin_12, LEVEL_SHIFTER.LV3
  N6: Pico.pin_16, SD_CARD_MODULE.pin_13
  N7: Pico.pin_17, SD_CARD_MODULE.pin_7
  N8: Pico.pin_19, SD_CARD_MODULE.pin_11, SD_CARD_MODULE.pin_12
  N9: Pico.pin_20, SD_CARD_MODULE.pin_9
  N10: Pico.pin_29, START/STOP.1
  N11: Pico.pin_30, RUN.3
  N12: Pico.pin_34, POT.S
  N13: Pico.pin_36, START/STOP.3, POT.A, SD_CARD_MODULE.pin_3, SD_CARD_MODULE.pin_4
  N14: Pico.pin_40, LEVEL_SHIFTER.HV, I2C_LCD_DISPLAY.VCC
  GND: LEVEL_SHIFTER.GND, I2C_LCD_DISPLAY.GND
  N15: LEVEL_SHIFTER.HV3, I2C_LCD_DISPLAY.SCL
  N16: LEVEL_SHIFTER.HV4, I2C_LCD_DISPLAY.SDA

custom parts:
  Raspberry Pi Pico: Raspberry Pi Pico. Based around the RP2040 microcontroller the Pico is a low cost microcontroller device bringing Raspberry Pi quality, cost, and easy of use to the microcontroller space. Jan 2021, Split part in to two versions: tht (this one) and SMD. This one will drill holes for a .1 in header in pcb to allow plugging in the module as well as providing pads to solder the module to the top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
  LCD1602-I2C: A standard character display, usually with 2x16 characters. Comes in many colors with LCM1602 IIC attached.
  Full Size SD Card Module: SD Card Module Slot Socket Reader For Arduino ARM MCU
